// Logisim project fig21.circ as structural Verilog: 1 circuit, main circuit main
module main (
  input  l0,
  input  l1,
  input  S,
  output Y
);

  wire and_1_out, and_2_out, not_1_out;

  not not_1 (not_1_out, S);
  and and_1 (and_1_out, l0, not_1_out);
  and and_2 (and_2_out, l1, S);
  or or_1 (Y, and_1_out, and_2_out);
endmodule
