// Logisim project fig22.circ as structural Verilog: 1 circuit, main circuit main
module main (
  input  x,
  output Y
);

  Multiplexer multiplexer_1 (.in0(1'b1), .in1(1'b0), .out(Y), .sel(x));
endmodule
