// Logisim project fig23.circ as structural Verilog: 1 circuit, main circuit main
module main (
  input  l0,
  input  l1,
  input  l2,
  input  l3,
  input  sel0,
  input  sel1,
  output Y
);

  wire multiplexer_1_out, multiplexer_3_out;

  Multiplexer multiplexer_1 (.in0(l0), .in1(l1), .out(multiplexer_1_out), .sel(sel0));
  Multiplexer multiplexer_2 (.in0(multiplexer_1_out), .in1(multiplexer_3_out), .out(Y), .sel(sel1));
  Multiplexer multiplexer_3 (.in0(l2), .in1(l3), .out(multiplexer_3_out), .sel(sel0));
endmodule
