// Logisim project full_adder.circ as structural Verilog: 1 circuit, main circuit main
module main (
  input  [2:0] in_1,
  output S,
  output Cout
);

  wire decoder_1_out0, decoder_1_out1, decoder_1_out2, decoder_1_out3, decoder_1_out4, decoder_1_out5,
       decoder_1_out6, decoder_1_out7;

  Decoder #(.enable("false"), .select(3)) decoder_1 (
    .out0(decoder_1_out0), .out1(decoder_1_out1), .out2(decoder_1_out2), .out3(decoder_1_out3),
    .out4(decoder_1_out4), .out5(decoder_1_out5), .out6(decoder_1_out6), .out7(decoder_1_out7), .sel(in_1));
  or or_1 (S, decoder_1_out7, decoder_1_out1, decoder_1_out2, decoder_1_out4);
  or or_2 (Cout, decoder_1_out3, decoder_1_out5, decoder_1_out6, decoder_1_out7);

  // Notes on the sheet:
  //   000
  //   001
  //   010
  //   011
  //   100
  //   101
  //   110
  //   111
endmodule
