// Logisim project ej4.circ as structural Verilog: 1 circuit, main circuit main
module main (
  input  [15:0] in_1,
  output [7:0] out_2
);

  wire decoder_1_out0, decoder_1_out2, not_1_out, not_2_out;
  wire [7:0] rom_1_data, rom_2_data, undriven;

  Decoder #(.select(2)) decoder_1 (
    .out0(decoder_1_out0), .out2(decoder_1_out2), .sel(in_1[15:14]));  // open: out1, out3, en
  not not_1 (not_1_out, decoder_1_out0);
  not not_2 (not_2_out, decoder_1_out2);
  ROM #(.addrWidth(13)) rom_1 (.addr(in_1[12:0]), .data(rom_1_data));
  ROM #(.addrWidth(12)) rom_2 (.addr(in_1[11:0]), .data(rom_2_data));
  Multiplexer #(.width(8)) multiplexer_1 (.in0(rom_1_data), .out(out_2), .sel(not_1_out));  // open: in1
  Multiplexer #(.width(8)) multiplexer_2 (.in0(rom_2_data), .in1(undriven), .out(out_2), .sel(not_2_out));

  // Notes on the sheet:
  //   contents of rom_1 (hex, n*v repeats v):
  //   11 0 0 1 0 0 0 11 0 0 0 1 0 0 0 1
  //   contents of rom_2 (hex, n*v repeats v):
  //   1f
endmodule
